// Logisim project s-mips.circ as structural Verilog
module S_MIPS_Board (
  input  DESHABILITAR_DISPATCHER,
  output halt
);

  wire button_1_out, CLK, CS, d_ff_1_q, LCLR, LoadRAM, LoadRAMOn, LW, R_R_W, R_W, ram_dispatcher_1_finished,
       RCS, Reset_out, RST, TTY_EN;
  wire [2:0] KDB;
  wire [3:0] LMask, Mask, ram_1_read_time, ram_1_write_time, RMask;
  wire [6:0] KDB_DATA, TTY_DATA;
  wire [15:0] Addr, LAddr, RAddr;
  wire [31:0] I0, I1, I2, I3, LData, ram_1_data_out_0, ram_1_data_out_1, ram_1_data_out_2, ram_1_data_out_3,
       RI0, RI1, RI2, RI3;

  TTY #(.rows(25), .cols(80)) tty_1 (.data(TTY_DATA), .clk(CLK), .we(TTY_EN), .clr(RST));
  not not_1 (LoadRAMOn, ram_dispatcher_1_finished);
  RAM_Dispatcher ram_dispatcher_1 (
    .WriteTime(ram_1_write_time), .Clock(CLK), .Data(LData), .Address(LAddr), .Mask(LMask),
    .Finished(ram_dispatcher_1_finished), .Write(LW), .CLR(LCLR));
  Keyboard #(.buflen(64)) keyboard_1 (.clk(CLK), .re(KDB[0]), .avail(KDB[2]), .data(KDB_DATA));  // open: clr
  RAM ram_1 (
    .Address(RAddr), .Data_Out_0(ram_1_data_out_0), .Data_Out_1(ram_1_data_out_1),
    .Data_Out_2(ram_1_data_out_2), .Data_Out_3(ram_1_data_out_3), .Data_In_0(RI0), .Data_In_1(RI1),
    .Data_In_2(RI2), .Data_In_3(RI3), .Mask(RMask), .nRead_Write(R_R_W), .Chip_Select(RCS),
    .Read_Time(ram_1_read_time), .Reset(button_1_out), .Write_Time(ram_1_write_time));
  Button button_1 (.out(button_1_out));
  D_Flip_Flop d_ff_1 (.clk(CLK), .D(1'b1), .Q(d_ff_1_q), .reset(Reset_out));  // open: Qn, preset, en
  Button Reset (.out(Reset_out));
  S_MIPS s_mips_1 (
    .Kbd_Enable(KDB[0]), .Address(Addr), .Kbd_Clear(KDB[1]), .Kbd_Available(KDB[2]), .RAM_In_0(I0),
    .Kbd_ASCII_Data(KDB_DATA), .RAM_In_1(I1), .TTY_Enable(TTY_EN), .RAM_In_2(I2), .RAM_In_3(I3),
    .TTY_ASCII_Data(TTY_DATA), .Reset(RST), .RAM_Out_0(ram_1_data_out_0), .Clock(CLK),
    .RAM_Out_1(ram_1_data_out_1), .Stop(halt), .RAM_Out_2(ram_1_data_out_2), .RAM_Out_3(ram_1_data_out_3),
    .Mask(Mask), .Read_Time(ram_1_read_time), .Write_Time(ram_1_write_time), .nRead_Write(R_W),
    .Chip_Select(CS));
  D_Flip_Flop d_ff_2 (.clk(CLK), .D(d_ff_1_q), .Qn(LCLR), .reset(Reset_out));  // open: Q, preset, en
  or or_1 (RST, LCLR, LoadRAM);
  Clock clock_1 (.out(CLK));
  Multiplexer #(.width(32), .enable("false")) multiplexer_1 (.in0(I0), .in1(LData), .out(RI0), .sel(LoadRAM));
  Multiplexer #(.width(32), .enable("false")) multiplexer_2 (.in0(I1), .in1(LData), .out(RI1), .sel(LoadRAM));
  Multiplexer #(.width(32), .enable("false")) multiplexer_3 (.in0(I2), .in1(LData), .out(RI2), .sel(LoadRAM));
  Multiplexer #(.width(32), .enable("false")) multiplexer_4 (.in0(I3), .in1(LData), .out(RI3), .sel(LoadRAM));
  and and_1 (LoadRAM, ~DESHABILITAR_DISPATCHER, LoadRAMOn);  // AND_Gate
  Multiplexer #(.width(16), .enable("false")) multiplexer_5 (.in0(Addr), .in1(LAddr), .out(RAddr), .sel(LoadRAM));
  Multiplexer #(.width(4), .enable("false")) multiplexer_6 (.in0(Mask), .in1(LMask), .out(RMask), .sel(LoadRAM));
  Multiplexer #(.enable("false")) multiplexer_7 (.in0(CS), .in1(LW), .out(RCS), .sel(LoadRAM));
  Multiplexer #(.enable("false")) multiplexer_8 (.in0(R_W), .in1(LW), .out(R_R_W), .sel(LoadRAM));

  // Notes on the sheet:
  //   NO MODIFICAR
  //   Keyboard
endmodule

module RAM (
  input  [15:0] Address,
  input  [31:0] Data_In_0,
  input  [31:0] Data_In_1,
  input  [31:0] Data_In_2,
  input  [31:0] Data_In_3,
  input  [3:0] Mask,
  input  nRead_Write,
  input  Chip_Select,
  input  Reset,
  output [31:0] Data_Out_0,
  output [31:0] Data_Out_1,
  output [31:0] Data_Out_2,
  output [31:0] Data_Out_3,
  output [3:0] Read_Time,
  output [3:0] Write_Time
);

  wire and_2_out, and_3_out, and_4_out, and_5_out, and_6_out, and_7_out, and_8_out, and_9_out, Changed, CLK,
       comparator_2_eq, comparator_3_eq, comparator_4_eq, comparator_5_eq, comparator_6_eq, Count,
       demultiplexer_3_out0, Idle, Idle_q, Load, Load0, Load1, nand_1_out, or_1_out, or_2_out, or_3_out,
       or_4_out, or_5_out, or_6_out, or_7_out, or_8_out, or_9_out, or_10_out, Proc_q, Update_Mem, Zero_Time;
  wire [3:0] counter_1_q, multiplexer_1_out, subtractor_1_out;
  wire [31:0] register_1_q, register_2_q, register_3_q, register_4_q, register_5_q;

  // Probe on 4'b0011
  // Probe on 4'b0010
  Multiplexer #(.width(4), .enable("false")) multiplexer_1 (
    .in0(4'b0011), .in1(4'b0010), .out(multiplexer_1_out), .sel(nRead_Write));
  or or_1 (or_1_out, Idle, Update_Mem);
  or or_2 (or_2_out, ~Chip_Select, Reset);  // OR_Gate
  Subtractor #(.width(4)) subtractor_1 (.a(multiplexer_1_out), .b(4'b0010), .out(subtractor_1_out));  // open: bin, bout
  D_Flip_Flop u_Idle (.clk(CLK), .D(or_1_out), .Q(Idle_q), .preset(or_2_out));  // open: Qn, en, reset
  Demultiplexer #(.enable("false")) demultiplexer_1 (.out0(Idle), .out1(Load0), .in(Idle_q), .sel(Changed));
  // Probe on counter_1_q
  Counter #(.width(4), .max('hf)) counter_1 (
    .load(Load), .D(subtractor_1_out), .count(Count), .Q(counter_1_q), .clk(CLK), .clr(or_3_out));  // open: carry
  or or_3 (or_3_out, ~Chip_Select, Reset);  // OR_Gate
  Comparator #(.width(4), .mode("unsigned")) comparator_1 (
    .a(4'b0000), .b(counter_1_q), .eq(Zero_Time));  // open: gt, lt
  or or_4 (or_4_out, Count, Load0, Load1);
  Register #(.width(32)) register_1 (.D(Data_In_0), .en(Chip_Select), .Q(register_1_q), .clk(CLK), .clr(or_5_out));
  or or_5 (or_5_out, ~Chip_Select, Reset);  // OR_Gate
  Register #(.width(32)) register_2 (.D(Data_In_1), .en(Chip_Select), .Q(register_2_q), .clk(CLK), .clr(or_6_out));
  or or_6 (or_6_out, ~Chip_Select, Reset);  // OR_Gate
  Register #(.width(32)) register_3 (.D(Data_In_2), .en(Chip_Select), .Q(register_3_q), .clk(CLK), .clr(or_7_out));
  or or_7 (or_7_out, ~Chip_Select, Reset);  // OR_Gate
  Register #(.width(32)) register_4 (.D(Data_In_3), .en(Chip_Select), .Q(register_4_q), .clk(CLK), .clr(or_8_out));
  or or_8 (or_8_out, ~Chip_Select, Reset);  // OR_Gate
  Register #(.width(32)) register_5 (
    .D({{11{1'b1}}, nRead_Write, Mask, Address}), .en(Chip_Select), .Q(register_5_q), .clk(CLK),
    .clr(or_9_out));
  or or_9 (or_9_out, ~Chip_Select, Reset);  // OR_Gate
  D_Flip_Flop Proc (.clk(CLK), .D(or_4_out), .Q(Proc_q), .reset(or_10_out));  // open: Qn, preset, en
  or or_10 (or_10_out, ~Chip_Select, Reset);  // OR_Gate
  Demultiplexer #(.enable("false")) demultiplexer_2 (
    .out0(Count), .out1(Update_Mem), .in(demultiplexer_3_out0), .sel(Zero_Time));
  Demultiplexer #(.enable("false")) demultiplexer_3 (
    .out0(demultiplexer_3_out0), .out1(Load1), .in(Proc_q), .sel(Changed));
  Clock clock_1 (.out(CLK));
  Comparator #(.width(32)) comparator_2 (.a(register_1_q), .b(Data_In_0), .eq(comparator_2_eq));  // open: gt, lt
  Comparator #(.width(32)) comparator_3 (.a(register_2_q), .b(Data_In_1), .eq(comparator_3_eq));  // open: gt, lt
  Comparator #(.width(32)) comparator_4 (.a(register_3_q), .b(Data_In_2), .eq(comparator_4_eq));  // open: gt, lt
  Comparator #(.width(32)) comparator_5 (.a(register_4_q), .b(Data_In_3), .eq(comparator_5_eq));  // open: gt, lt
  Comparator #(.width(32)) comparator_6 (
    .a(register_5_q), .b({{11{1'b1}}, nRead_Write, Mask, Address}), .eq(comparator_6_eq));  // open: gt, lt
  nand nand_1 (nand_1_out, comparator_6_eq, comparator_2_eq, comparator_3_eq, comparator_4_eq, comparator_5_eq);
  and and_1 (Changed, nand_1_out, Chip_Select);
  or or_11 (Load, Count, Load1, Load0);
  and and_2 (and_2_out, Mask[0], Update_Mem, nRead_Write);
  and and_3 (and_3_out, Mask[1], Update_Mem, nRead_Write);
  and and_4 (and_4_out, Mask[2], Update_Mem, nRead_Write);
  and and_5 (and_5_out, Mask[3], Update_Mem, nRead_Write);
  RAM_part #(.addrWidth(16), .dataWidth(32), .bus("separate")) ram_1 (
    .addr(Address), .din(Data_In_0), .data(Data_Out_0), .str(and_2_out), .sel(Chip_Select), .clk(CLK),
    .ld(and_6_out), .clr(Reset));
  and and_6 (and_6_out, ~nRead_Write, Idle);  // AND_Gate
  RAM_part #(.addrWidth(16), .dataWidth(32), .bus("separate")) ram_2 (
    .addr(Address), .din(Data_In_1), .data(Data_Out_1), .str(and_3_out), .sel(Chip_Select), .clk(CLK),
    .ld(and_7_out), .clr(Reset));
  and and_7 (and_7_out, ~nRead_Write, Idle);  // AND_Gate
  RAM_part #(.addrWidth(16), .dataWidth(32), .bus("separate")) ram_3 (
    .addr(Address), .din(Data_In_2), .data(Data_Out_2), .str(and_4_out), .sel(Chip_Select), .clk(CLK),
    .ld(and_8_out), .clr(Reset));
  and and_8 (and_8_out, ~nRead_Write, Idle);  // AND_Gate
  RAM_part #(.addrWidth(16), .dataWidth(32), .bus("separate")) ram_4 (
    .addr(Address), .din(Data_In_3), .data(Data_Out_3), .str(and_5_out), .sel(Chip_Select), .clk(CLK),
    .ld(and_9_out), .clr(Reset));
  and and_9 (and_9_out, ~nRead_Write, Idle);  // AND_Gate

  assign Read_Time = 4'b0011;
  assign Write_Time = 4'b0010;

  // Other names for the same wires on the sheet: M0 = Mask[0]; M1 = Mask[1]; M2 = Mask[2]; M3 = Mask[3];
  //   RW = nRead_Write; CLR = Reset; CS = Chip_Select; Load2 = Count

  // Notes on the sheet:
  //   NO MODIFICAR
  //   excepto quizás los valores RT y WT
  //   BANK0
  //   BANK1
  //   BANK2
  //   BANK3
endmodule

module S_MIPS (
  input  Kbd_Available,
  input  [6:0] Kbd_ASCII_Data,
  input  [31:0] RAM_Out_0,
  input  [31:0] RAM_Out_1,
  input  Reset,
  input  [31:0] RAM_Out_2,
  input  Clock,
  input  [31:0] RAM_Out_3,
  input  [3:0] Read_Time,
  input  [3:0] Write_Time,
  output Kbd_Enable,
  output [15:0] Address,
  output Kbd_Clear,
  output TTY_Enable,
  output [6:0] TTY_ASCII_Data,
  output Stop,
  output [3:0] Mask,
  output [31:0] RAM_In_0,
  output [31:0] RAM_In_1,
  output nRead_Write,
  output Chip_Select,
  output [31:0] RAM_In_2,
  output [31:0] RAM_In_3
);

  wire get_data, get_inst, GNI, L_GI, L_PC, L_RF, or_1_out, ready_data, ready_inst, ready_write, start,
       tty_inst, write;
  wire [2:0] CU_select;
  wire [31:0] address_t, instruction, multiplexer_1_out, multiplexer_2_out, multiplexer_3_out,
       multiplexer_4_out, read_write_ram_1_out_14, read_write_ram_1_out_15, read_write_ram_1_out_16,
       read_write_ram_1_out_17;

  D_Flip_Flop #(.trigger("falling")) d_ff_1 (.clk(Clock), .D(Reset), .Q(start));  // open: Qn, preset, en, reset
  D_Flip_Flop #(.trigger("falling")) d_ff_2 (
    .clk(Clock), .D(get_inst), .Q(GNI), .en(or_1_out));  // open: Qn, preset, reset
  or or_1 (or_1_out, get_inst, ready_inst);
  Multiplexer #(.width(32), .enable("false")) multiplexer_1 (
    .in0(RAM_Out_0), .in1(RAM_In_0), .out(multiplexer_1_out), .sel(write));
  Multiplexer #(.width(32), .enable("false")) multiplexer_2 (
    .in0(RAM_Out_1), .in1(RAM_In_0), .out(multiplexer_2_out), .sel(write));
  Multiplexer #(.width(32), .enable("false")) multiplexer_3 (
    .in0(RAM_Out_2), .in1(RAM_In_0), .out(multiplexer_3_out), .sel(write));
  Multiplexer #(.width(32), .enable("false")) multiplexer_4 (
    .in0(RAM_Out_3), .in1(RAM_In_0), .out(multiplexer_4_out), .sel(write));
  Data_Path_2 data_path_1 (
    .in_5(Clock), .in_3(L_RF), .in_6(Reset), .in_7(L_GI), .in_4(L_PC), .in_2(Kbd_ASCII_Data),
    .Output_2(TTY_ASCII_Data), .in_8(GNI), .out_11(CU_select), .Output(address_t), .out_13(tty_inst),
    .R_out({RAM_In_0[7:0], RAM_In_0[15:8], RAM_In_0[23:16], RAM_In_0[31:24]}), .in_1(instruction));
  Read_Write_RAM read_write_ram_1 (
    .in_1(multiplexer_1_out), .in_2(multiplexer_2_out), .in_3(multiplexer_3_out), .in_4(multiplexer_4_out),
    .in_5(address_t), .in_6(Read_Time), .in_7(Write_Time), .in_13(Reset), .in_10(write), .in_8(get_inst),
    .in_9(get_data), .in_11(L_GI), .out_14(read_write_ram_1_out_14), .out_15(read_write_ram_1_out_15),
    .out_16(read_write_ram_1_out_16), .out_17(read_write_ram_1_out_17), .out_18(Address), .out_19(Mask),
    .cs(Chip_Select), .out_24(nRead_Write), .out_20(ready_inst), .out_21(ready_data), .out_22(ready_write),
    .in_12(Clock));
  Control_Unit control_unit_1 (
    .in_4(start), .in_6(ready_inst), .in_3(Reset), .in_2(tty_inst), .in_5(ready_data), .in_7(CU_select),
    .out_9(L_RF), .out_11(L_PC), .out_13(Stop), .out_15(get_data), .out_10(get_inst), .out_12(L_GI),
    .out_14(TTY_Enable), .out_16(Kbd_Enable), .out_17(write), .in_1(Clock), .in_8(ready_write));
  Multiplexer #(.select(2), .width(32), .enable("false")) multiplexer_5 (
    .in0(read_write_ram_1_out_14), .in1(read_write_ram_1_out_15), .in2(read_write_ram_1_out_16),
    .in3(read_write_ram_1_out_17), .out(instruction), .sel(address_t[3:2]));

  assign Kbd_Clear = Reset;
  assign RAM_In_1 = RAM_In_0;
  assign RAM_In_2 = RAM_In_0;
  assign RAM_In_3 = RAM_In_0;

  // Other names for the same wires on the sheet: CLK = Clock; CLR = Reset; CS = Chip_Select;
  //   KBD_AVAIL = Kbd_Available; KBD_DATA[6:0] = Kbd_ASCII_Data; L_KBD = Kbd_Enable; L_TTY = TTY_Enable;
  //   RAM_A[15:0] = Address; RAM_MASK[3:0] = Mask; RAM_OUTPUT_0[31:0] = RAM_Out_0; RAM_OUTPUT_1[31:0] = RAM_Out_1;
  //   RAM_OUTPUT_2[31:0] = RAM_Out_2; RAM_OUTPUT_3[31:0] = RAM_Out_3; RW = nRead_Write;
  //   TTY_DATA[6:0] = TTY_ASCII_Data; RAM_INPUT_0[31:0] = RAM_In_0; RAM_INPUT_1[31:0] = RAM_In_0;
  //   RAM_INPUT_2[31:0] = RAM_In_0; RAM_INPUT_3[31:0] = RAM_In_0; write_out[31:0] = RAM_In_0

  // Notes on the sheet:
  //   RAM ADDRESS
  //   DATA FROM RAM
  //   DATA TO RAM
  //   RAM TIMING
  //   RAM CONTROL
  //   KEYBOARD
  //   TTY
  //   SEQUENCING
  //   DATA WRITE MASK
endmodule

module RAM_Dispatcher (
  input  [3:0] WriteTime,
  input  Clock,
  input  CLR,
  output [31:0] Data,
  output [15:0] Address,
  output [3:0] Mask,
  output Finished,
  output Write
);

  wire demultiplexer_2_out1, demultiplexer_3_out1, End, IDLE_q, IncAddr, Load, or_1_out, or_2_out, While_q,
       WriteEnd;
  wire [3:0] counter_1_q;
  wire [31:0] CurrentAddress_q;

  Counter #(.width(32), .max('hffffffff)) CurrentAddress (
    .count(IncAddr), .Q({CurrentAddress_q[31:18], Address, CurrentAddress_q[1:0]}), .clk(Clock), .clr(CLR));  // open: load, D, carry
  or or_1 (or_1_out, IncAddr, demultiplexer_3_out1, Finished);
  D_Flip_Flop IDLE (.clk(Clock), .D(or_1_out), .Q(IDLE_q), .preset(CLR));  // open: Qn, en, reset
  Demultiplexer #(.enable("false")) demultiplexer_1 (.out0(Load), .out1(Finished), .in(IDLE_q), .sel(End));
  D_Flip_Flop While (.clk(Clock), .D(or_2_out), .Q(While_q), .reset(CLR));  // open: Qn, preset, en
  or or_2 (or_2_out, Write, Load);
  RAM_part #(.addrWidth(18), .dataWidth(32)) ram_1 (
    .addr({Address, CurrentAddress_q[1:0]}), .data(Data), .clk(Clock));  // open: sel, ld, clr
  Demultiplexer #(.enable("false")) demultiplexer_2 (
    .out0(Write), .out1(demultiplexer_2_out1), .in(While_q), .sel(WriteEnd));
  Decoder #(.select(2)) decoder_1 (
    .out0(Mask[0]), .out1(Mask[1]), .out2(Mask[2]), .out3(Mask[3]), .sel(CurrentAddress_q[1:0]));  // open: en
  Demultiplexer #(.enable("false")) demultiplexer_3 (
    .out0(IncAddr), .out1(demultiplexer_3_out1), .in(demultiplexer_2_out1), .sel(End));
  Counter #(.width(4), .max('hf)) counter_1 (
    .load(Load), .D(WriteTime), .count(Write), .Q(counter_1_q), .clk(Clock));  // open: carry, clr
  Comparator #(.width(32)) comparator_1 (.a(Data), .b({32{1'b1}}), .eq(End));  // open: gt, lt
  Comparator #(.width(4)) comparator_2 (.a(4'b0000), .b(counter_1_q), .eq(WriteEnd));  // open: gt, lt

  // Other names for the same wires on the sheet: CLK = Clock; Count = Write; WT[3:0] = WriteTime
endmodule

module multiplier (
  input  [31:0] in_1,
  input  in_2,
  input  [31:0] in_3,
  output [31:0] Output,
  output [31:0] Output_2
);

  wire adder_1_cout, adder_3_cout, adder_5_cout, and_1_out, c1, c2, ca, cb;
  wire [31:0] a_2, a_cb, adder_1_out, adder_2_out, adder_3_out, adder_4_out, and_2_out, and_3_out, b_2, b_ca,
       bit_extender_1_out, bit_extender_2_out, c_ab, HI, HIU, LO, LOU, multiplier_2_cout, multiplier_2_out,
       shift_left_2_out_3, shift_left_3_out_3, shift_left_4_out_3, shift_left_out_3;

  SHR shr_1 (.in_1(in_1), .out_3(a_2), .Output(ca), .in_2(1'b0));
  and and_1 (and_1_out, ca, cb);
  assign bit_extender_1_out = {{31{cb}}, cb};  // Bit_Extender bit_extender_1
  assign bit_extender_2_out = {{31{ca}}, ca};  // Bit_Extender bit_extender_2
  assign c_ab = {{31{1'b0}}, and_1_out};  // Bit_Extender bit_extender_3
  assign and_2_out = a_2 & bit_extender_1_out;  // AND_Gate and_2, 32 bits wide
  assign and_3_out = b_2 & bit_extender_2_out;  // AND_Gate and_3, 32 bits wide
  SHR shr_2 (.in_1(in_3), .out_3(b_2), .Output(cb), .in_2(1'b0));
  SHL shl_1 (.in_1(and_2_out), .out_3(a_cb), .in_2(1'b0));  // open: Output
  SHL shl_2 (.in_1(and_3_out), .out_3(b_ca), .in_2(1'b0));  // open: Output
  Multiplier #(.width(32)) multiplier_1 (.a(in_1), .b(in_3), .out(LO), .cout(HI));  // open: cin
  SHL shift_left (.in_1(multiplier_2_out), .out_3(shift_left_out_3), .Output(c1), .in_2(1'b0));
  Multiplier #(.width(32)) multiplier_2 (
    .a(a_2), .b(b_2), .out(multiplier_2_out), .cout(multiplier_2_cout));  // open: cin
  SHL shift_left_2 (.in_1(multiplier_2_cout), .out_3(shift_left_2_out_3), .in_2(c1));  // open: Output
  SHL shift_left_3 (.in_1(shift_left_out_3), .out_3(shift_left_3_out_3), .Output(c2), .in_2(1'b0));
  SHL shift_left_4 (.in_1(shift_left_2_out_3), .out_3(shift_left_4_out_3), .in_2(c2));  // open: Output
  // Probe on HIU
  Multiplexer #(.width(32), .enable("false")) multiplexer_1 (.in0(HIU), .in1(HI), .out(Output), .sel(in_2));
  Multiplexer #(.width(32), .enable("false")) multiplexer_2 (.in0(LOU), .in1(LO), .out(Output_2), .sel(in_2));
  Adder #(.width(32)) adder_1 (.a(shift_left_3_out_3), .b(a_cb), .out(adder_1_out), .cout(adder_1_cout));  // open: cin
  Adder #(.width(32)) adder_2 (
    .a(shift_left_4_out_3), .b({32{1'b0}}), .out(adder_2_out), .cin(adder_1_cout));  // open: cout
  Adder #(.width(32)) adder_3 (.a(adder_1_out), .b(b_ca), .out(adder_3_out), .cout(adder_3_cout));  // open: cin
  Adder #(.width(32)) adder_4 (.a(adder_2_out), .b({32{1'b0}}), .out(adder_4_out), .cin(adder_3_cout));  // open: cout
  Adder #(.width(32)) adder_5 (.a(adder_3_out), .b(c_ab), .out(LOU), .cout(adder_5_cout));  // open: cin
  Adder #(.width(32)) adder_6 (.a(adder_4_out), .b({32{1'b0}}), .out(HIU), .cin(adder_5_cout));  // open: cout

  // Other names for the same wires on the sheet: a[31:0] = in_1; b[31:0] = in_3; sign = in_2
endmodule

module SHR (
  input  [31:0] in_1,
  input  in_2,
  output [31:0] out_3,
  output Output
);


  assign out_3 = {in_2, in_1[31:1]};
  assign Output = in_1[0];

  // Other names for the same wires on the sheet: a[31:0] = in_1; a_2[31:0] = {in_2, in_1[31:1]}
endmodule

module SHL (
  input  [31:0] in_1,
  input  in_2,
  output [31:0] out_3,
  output Output
);


  assign out_3 = {in_1[30:0], in_2};
  assign Output = in_1[31];

  // Other names for the same wires on the sheet: a[31:0] = in_1; a_2[31:0] = {in_1[30:0], in_2}
endmodule

module divider (
  input  [31:0] in_1,
  input  in_2,
  input  [31:0] in_3,
  output [31:0] out_4,
  output [31:0] out_5
);

  wire neg_a, neg_b, neg_div, xor_2_out;
  wire [31:0] abs_a, abs_b, abs_div, adder_1_out, multiplexer_3_out, negator_1_out, negator_2_out,
       negator_3_out, negator_4_out, R, res, subtractor_1_out;

  Negator #(.width(32)) negator_1 (.in(in_1), .out(negator_1_out));
  Negator #(.width(32)) negator_2 (.in(in_3), .out(negator_2_out));
  and and_1 (neg_a, in_1[31], in_2);
  and and_2 (neg_b, in_2, in_3[31]);
  Multiplexer #(.width(32), .enable("false")) multiplexer_1 (.in0(in_1), .in1(negator_1_out), .out(abs_a), .sel(neg_a));
  Multiplexer #(.width(32), .enable("false")) multiplexer_2 (.in0(in_3), .in1(negator_2_out), .out(abs_b), .sel(neg_b));
  Divider #(.width(32)) divider_1 (.a(abs_a), .b(abs_b), .out(res), .rem(R));  // open: upper
  xor xor_1 (neg_div, neg_a, neg_b);
  Adder #(.width(32)) adder_1 (.a(res), .b(32'h1), .out(adder_1_out));  // open: cin, cout
  Multiplexer #(.width(32), .enable("false")) multiplexer_3 (
    .in0(res), .in1(adder_1_out), .out(multiplexer_3_out), .sel(neg_a));
  Multiplexer #(.width(32), .enable("false")) multiplexer_4 (
    .in0(multiplexer_3_out), .in1(negator_3_out), .out(abs_div), .sel(xor_2_out));
  Negator #(.width(32)) negator_3 (.in(multiplexer_3_out), .out(negator_3_out));
  xor xor_2 (xor_2_out, neg_a, neg_b);
  Multiplexer #(.width(32), .enable("false")) multiplexer_5 (
    .in0(abs_div), .in1(negator_4_out), .out(out_4), .sel(neg_div));
  Negator #(.width(32)) negator_4 (.in(abs_div), .out(negator_4_out));
  Subtractor #(.width(32)) subtractor_1 (.a(abs_b), .b(R), .out(subtractor_1_out));  // open: bin, bout
  Multiplexer #(.width(32), .enable("false")) multiplexer_6 (.in0(R), .in1(subtractor_1_out), .out(out_5), .sel(neg_a));

  // Other names for the same wires on the sheet: a[31:0] = in_1; b[31:0] = in_3; div[31:0] = out_4;
  //   remainder[31:0] = out_5; sign = in_2
endmodule

module ALU_2 (
  input  [31:0] Input,
  input  [31:0] Input_2,
  input  [3:0] in_3,
  input  in_4,
  input  in_5,
  output [31:0] out_6,
  output [31:0] out_7,
  output [31:0] out_8
);

  wire div, enable, mult;
  wire [31:0] add, \and , div_rem, div_res, mult_high, mult_low, multiplexer_1_out, multiplexer_2_out, \nor ,
       \or , slt, sub, \xor ;

  assign \and  = Input & Input_2;  // AND_Gate and_1, 32 bits wide
  assign \or  = Input | Input_2;  // OR_Gate or_1, 32 bits wide
  assign \nor  = ~(Input | Input_2);  // NOR_Gate nor_1, 32 bits wide
  assign \xor  = Input ^ Input_2;  // XOR_Gate xor_1, 32 bits wide
  Adder #(.width(32)) adder_1 (.a(Input), .b(Input_2), .out(add));  // open: cin, cout
  Subtractor #(.width(32)) subtractor_1 (.a(Input), .b(Input_2), .out(sub));  // open: bin, bout
  Sltu sltu_1 (.in_1(Input), .in_3(in_4), .in_2(Input_2), .out_4(slt));
  divider divider_1 (.in_1(Input), .in_2(in_4), .in_3(Input_2), .out_4(div_res), .out_5(div_rem));
  multiplier multiplier_1 (.in_1(Input), .in_2(in_4), .in_3(Input_2), .Output(mult_high), .Output_2(mult_low));
  and and_2 (mult, ~in_3[0], in_3[1], ~in_3[2], ~in_3[3]);  // AND_Gate
  and and_3 (div, in_3[0], in_3[1], ~in_3[2], ~in_3[3]);  // AND_Gate
  or or_2 (enable, mult, div);
  Multiplexer #(.width(32), .enable("false")) multiplexer_1 (
    .in0(mult_low), .in1(div_res), .out(multiplexer_1_out), .sel(div));
  Multiplexer #(.width(32), .enable("false")) multiplexer_2 (
    .in0(mult_high), .in1(div_rem), .out(multiplexer_2_out), .sel(div));
  Register #(.width(32)) register_1 (.D(multiplexer_1_out), .en(enable), .Q(out_7), .clk(in_5));  // open: clr
  Register #(.width(32)) register_2 (.D(multiplexer_2_out), .en(enable), .Q(out_8), .clk(in_5));  // open: clr
  Multiplexer #(.select(4), .width(32), .enable("false")) multiplexer_3 (
    .in0(add), .in1(sub), .in4(slt), .in5(\and ), .in6(\or ), .in7(\nor ), .in8(\xor ), .out(out_6),
    .sel(in_3));  // open: in2, in3, in9, in10, in11, in12, in13, in14, in15

  // Other names for the same wires on the sheet: a[31:0] = Input; b[31:0] = Input_2; clock = in_5; HI[31:0] = out_8;
  //   LO[31:0] = out_7; _0 = in_3[0]; selector[3:0] = in_3; _1 = in_3[1]; _2 = in_3[2]; _3 = in_3[3]; sign = in_4
endmodule

module Sltu (
  input  [31:0] in_1,
  input  [31:0] in_2,
  input  in_3,
  output [31:0] out_4
);

  wire multiplexer_1_out, slt, sltu;

  Comparator #(.width(32)) comparator_1 (.a(in_1), .b(in_2), .lt(slt));  // open: gt, eq
  Comparator #(.width(32), .mode("unsigned")) comparator_2 (.a(in_1), .b(in_2), .lt(sltu));  // open: gt, eq
  Multiplexer #(.enable("false")) multiplexer_1 (.in0(sltu), .in1(slt), .out(multiplexer_1_out), .sel(in_3));
  assign out_4 = {{31{1'b0}}, multiplexer_1_out};  // Bit_Extender bit_extender_1

  // Other names for the same wires on the sheet: a[31:0] = in_1; b[31:0] = in_2; sign = in_3
endmodule

module ALU_selector (
  input  in_1,
  input  in_2,
  input  in_3,
  input  in_4,
  input  in_5,
  input  in_6,
  input  in_7,
  input  in_8,
  input  in_9,
  input  in_10,
  input  in_11,
  input  in_12,
  input  in_13,
  input  in_14,
  input  in_15,
  input  in_16,
  input  in_17,
  output sign,
  output I,
  output [3:0] selector
);

  wire AND, DIV, MUL, OR, SLT, SLTI;

  or or_1 (MUL, in_6, in_9);
  or or_2 (DIV, in_12, in_15);
  or or_3 (SLT, in_1, in_4);
  or or_4 (SLTI, in_5, in_8);
  or or_5 (selector[0], in_3, DIV, AND, in_13);
  or or_6 (AND, in_7, in_11);
  or or_7 (OR, in_10, in_14);
  or or_8 (selector[3], in_16, in_17);
  or or_9 (selector[1], MUL, DIV, OR, in_13);
  or or_10 (selector[2], SLT, SLTI, OR, AND, in_13);
  or or_11 (sign, in_6, in_12, in_1, in_5);
  or or_12 (I, in_2, SLTI, in_11, in_14, in_17);

  // Other names for the same wires on the sheet: addi = in_2; and_t = in_7; andi = in_11; div_t = in_12; divu = in_15;
  //   mul_t = in_6; mulu = in_9; nor = in_13; or_t = in_10; ori = in_14; _0 = selector[0]; _1 = selector[1];
  //   _2 = selector[2]; _3 = selector[3]; XOR = selector[3]; slt_t = in_1; slti_t = in_5; sltiu = in_8; sltu = in_4;
  //   sub = in_3; xor_t = in_16; xori = in_17
endmodule

module Register_File (
  input  [31:0] in_1,
  input  [4:0] in_2,
  input  [4:0] in_3,
  input  [4:0] in_4,
  input  in_5,
  input  in_6,
  input  in_7,
  input  in_8,
  input  in_9,
  input  in_10,
  output [31:0] out_11,
  output [31:0] out_12,
  output [31:0] out_13
);

  wire and_1_out, L0, L1, L2, L3, L4, L5, L6, L7, L8, L9, L10, L11, L12, L13, L14, L15, L16, L17, L18, L19,
       L20, L21, L22, L23, L24, L25, L26, L27, L28, L29, L30, L31, L31_1, or_1_out;
  wire [31:0] adder_1_out, multiplexer_1_out, multiplexer_2_out, out0, out1, out2, out3, out4, out5, out6,
       out7, out8, out9, out10, out11, out12, out13, out14, out15, out16, out17, out18, out19, out20, out21,
       out22, out23, out24, out25, out26, out27, out28, out29, out30, SP, subtractor_1_out;

  Demultiplexer #(.select(5), .enable("false")) demultiplexer_1 (
    .out0(L0), .out1(L1), .out2(L2), .out3(L3), .out4(L4), .out5(L5), .out6(L6), .out7(L7), .out8(L8),
    .out9(L9), .out10(L10), .out11(L11), .out12(L12), .out13(L13), .out14(L14), .out15(L15), .out16(L16),
    .out17(L17), .out18(L18), .out19(L19), .out20(L20), .out21(L21), .out22(L22), .out23(L23), .out24(L24),
    .out25(L25), .out26(L26), .out27(L27), .out28(L28), .out29(L29), .out30(L30), .out31(L31_1), .in(in_6),
    .sel(in_2));
  or or_1 (or_1_out, in_7, in_8);
  and and_1 (and_1_out, or_1_out, in_5);
  Register #(.width(32)) register_1 (.D({32{1'b0}}), .en(L0), .Q(out0), .clk(in_9), .clr(in_10));
  Register #(.width(32)) register_2 (.D(in_1), .en(L4), .Q(out4), .clk(in_9), .clr(in_10));
  Register #(.width(32)) register_3 (.D(in_1), .en(L8), .Q(out8), .clk(in_9), .clr(in_10));
  Register #(.width(32)) register_4 (.D(in_1), .en(L12), .Q(out12), .clk(in_9), .clr(in_10));
  Register #(.width(32)) register_5 (.D(in_1), .en(L16), .Q(out16), .clk(in_9), .clr(in_10));
  Register #(.width(32)) register_6 (.D(in_1), .en(L20), .Q(out20), .clk(in_9), .clr(in_10));
  Register #(.width(32)) register_7 (.D(in_1), .en(L24), .Q(out24), .clk(in_9), .clr(in_10));
  Register #(.width(32)) register_8 (.D(in_1), .en(L28), .Q(out28), .clk(in_9), .clr(in_10));
  or or_2 (L31, and_1_out, L31_1, in_10);
  Register #(.width(32)) register_9 (.D(in_1), .en(L1), .Q(out1), .clk(in_9), .clr(in_10));
  Register #(.width(32)) register_10 (.D(in_1), .en(L5), .Q(out5), .clk(in_9), .clr(in_10));
  Register #(.width(32)) register_11 (.D(in_1), .en(L9), .Q(out9), .clk(in_9), .clr(in_10));
  Register #(.width(32)) register_12 (.D(in_1), .en(L13), .Q(out13), .clk(in_9), .clr(in_10));
  Register #(.width(32)) register_13 (.D(in_1), .en(L17), .Q(out17), .clk(in_9), .clr(in_10));
  Register #(.width(32)) register_14 (.D(in_1), .en(L21), .Q(out21), .clk(in_9), .clr(in_10));
  Register #(.width(32)) register_15 (.D(in_1), .en(L25), .Q(out25), .clk(in_9), .clr(in_10));
  Register #(.width(32)) register_16 (.D(in_1), .en(L29), .Q(out29), .clk(in_9), .clr(in_10));
  Register #(.width(32)) register_17 (.D(in_1), .en(L2), .Q(out2), .clk(in_9), .clr(in_10));
  Register #(.width(32)) register_18 (.D(in_1), .en(L6), .Q(out6), .clk(in_9), .clr(in_10));
  Register #(.width(32)) register_19 (.D(in_1), .en(L10), .Q(out10), .clk(in_9), .clr(in_10));
  Register #(.width(32)) register_20 (.D(in_1), .en(L14), .Q(out14), .clk(in_9), .clr(in_10));
  Register #(.width(32)) register_21 (.D(in_1), .en(L18), .Q(out18), .clk(in_9), .clr(in_10));
  Register #(.width(32)) register_22 (.D(in_1), .en(L22), .Q(out22), .clk(in_9), .clr(in_10));
  Register #(.width(32)) register_23 (.D(in_1), .en(L26), .Q(out26), .clk(in_9), .clr(in_10));
  Register #(.width(32)) register_24 (.D(in_1), .en(L30), .Q(out30), .clk(in_9), .clr(in_10));
  Subtractor #(.width(32)) subtractor_1 (.a(out_13), .b(32'h4), .out(subtractor_1_out));  // open: bin, bout
  Multiplexer #(.width(32), .enable("false")) multiplexer_1 (
    .in0(subtractor_1_out), .in1(adder_1_out), .out(multiplexer_1_out), .sel(in_8));
  Adder #(.width(32)) adder_1 (.a(32'h4), .b(out_13), .out(adder_1_out));  // open: cin, cout
  Register #(.width(32)) register_25 (.D(in_1), .en(L3), .Q(out3), .clk(in_9), .clr(in_10));
  Register #(.width(32)) register_26 (.D(in_1), .en(L7), .Q(out7), .clk(in_9), .clr(in_10));
  Register #(.width(32)) register_27 (.D(in_1), .en(L11), .Q(out11), .clk(in_9), .clr(in_10));
  Register #(.width(32)) register_28 (.D(in_1), .en(L15), .Q(out15), .clk(in_9), .clr(in_10));
  Register #(.width(32)) register_29 (.D(in_1), .en(L19), .Q(out19), .clk(in_9), .clr(in_10));
  Register #(.width(32)) register_30 (.D(in_1), .en(L23), .Q(out23), .clk(in_9), .clr(in_10));
  Register #(.width(32)) register_31 (.D(in_1), .en(L27), .Q(out27), .clk(in_9), .clr(in_10));
  Register #(.width(32)) register_32 (.D(SP), .en(L31), .Q(out_13), .clk(in_9));  // open: clr
  Multiplexer #(.width(32), .enable("false")) multiplexer_2 (
    .in0(multiplexer_1_out), .in1({32{1'b0}}), .out(multiplexer_2_out), .sel(in_10));
  Multiplexer #(.width(32), .enable("false")) multiplexer_3 (
    .in0(multiplexer_2_out), .in1(in_1), .out(SP), .sel(L31_1));
  Multiplexer #(.select(5), .width(32), .enable("false")) multiplexer_4 (
    .in0(out0), .in1(out1), .in2(out2), .in3(out3), .in4(out4), .in5(out5), .in6(out6), .in7(out7),
    .in8(out8), .in9(out9), .in10(out10), .in11(out11), .in12(out12), .in13(out13), .in14(out14),
    .in15(out15), .in16(out16), .in17(out17), .in18(out18), .in19(out19), .in20(out20), .in21(out21),
    .in22(out22), .in23(out23), .in24(out24), .in25(out25), .in26(out26), .in27(out27), .in28(out28),
    .in29(out29), .in30(out30), .in31(out_13), .out(out_11), .sel(in_3));
  Multiplexer #(.select(5), .width(32), .enable("false")) multiplexer_5 (
    .in0(out0), .in1(out1), .in2(out2), .in3(out3), .in4(out4), .in5(out5), .in6(out6), .in7(out7),
    .in8(out8), .in9(out9), .in10(out10), .in11(out11), .in12(out12), .in13(out13), .in14(out14),
    .in15(out15), .in16(out16), .in17(out17), .in18(out18), .in19(out19), .in20(out20), .in21(out21),
    .in22(out22), .in23(out23), .in24(out24), .in25(out25), .in26(out26), .in27(out27), .in28(out28),
    .in29(out29), .in30(out30), .in31(out_13), .out(out_12), .sel(in_4));

  // Other names for the same wires on the sheet: A_select[4:0] = in_3; B_select[4:0] = in_4; clock = in_9;
  //   input[31:0] = in_1; L_PC = in_5; out31[31:0] = out_13; pop = in_8; push = in_7; reset = in_10;
  //   select[4:0] = in_2; write = in_6
endmodule

module RF_Input (
  input  [6:0] in_1,
  input  [31:0] in_2,
  input  [2:0] in_3,
  input  [31:0] in_4,
  input  [31:0] in_5,
  input  [31:0] in_6,
  input  [31:0] in_7,
  output [31:0] Output
);

  Multiplexer #(.select(3), .width(32), .enable("false")) multiplexer_1 (
    .in0(in_2), .in1(in_5), .in2(in_6), .in3(in_7), .in4(in_4), .in5({{25{1'b0}}, in_1}), .out(Output),
    .sel(in_3));  // open: in6, in7

  // Other names for the same wires on the sheet: ALU[31:0] = in_2; HI[31:0] = in_6; KBD[6:0] = in_1; LO[31:0] = in_7;
  //   memoryA[31:0] = in_5; RND[31:0] = in_4; selector[2:0] = in_3
endmodule

module Instruction_Decoder (
  input  [31:0] in_1,
  output [25:0] out_2,
  output [31:0] out_3,
  output [15:0] out_4,
  output [4:0] out_5,
  output [4:0] out_6,
  output [4:0] out_7,
  output [3:0] out_8,
  output [2:0] out_9,
  output [2:0] out_10,
  output out_11,
  output out_12,
  output out_13,
  output out_14,
  output out_15,
  output out_16,
  output out_17,
  output out_18,
  output out_19,
  output out_20,
  output out_21,
  output out_22,
  output out_23,
  output out_24,
  output out_25
);

  wire _000000, _111111, ADD, add_t, addi, ALU_inst, AND, and_t, andi, comparator_17_eq, comparator_18_eq,
       comparator_19_eq, comparator_20_eq, comparator_21_eq, comparator_22_eq, comparator_23_eq,
       comparator_24_eq, comparator_25_eq, comparator_26_eq, comparator_27_eq, comparator_28_eq,
       comparator_29_eq, comparator_30_eq, comparator_31_eq, comparator_32_eq, comparator_33_eq,
       comparator_34_eq, comparator_35_eq, comparator_36_eq, comparator_37_eq, comparator_38_eq,
       comparator_39_eq, comparator_40_eq, DIV, div_t, divu, halt, jmp_inst, kbd, mem_inst, mfhi, mflo, MUL,
       mult, mulu, nop, \nor , OR, or_21_out, or_t, ori, R_inst, SLT, slt_t, SLTI, slti_t, sltiu, sltu,
       stack_inst, sub, write_inst, XOR, xor_t, xori;

  Comparator #(.width(6)) comparator_1 (.a(in_1[31:26]), .b(6'b001000), .eq(addi));  // open: gt, lt
  Comparator #(.width(6)) comparator_2 (.a(in_1[31:26]), .b(6'b001010), .eq(slti_t));  // open: gt, lt
  Comparator #(.width(6)) comparator_3 (.a(in_1[31:26]), .b(6'b001011), .eq(sltiu));  // open: gt, lt
  Comparator #(.width(6)) comparator_4 (.a(in_1[31:26]), .b(6'b001100), .eq(andi));  // open: gt, lt
  Comparator #(.width(6)) comparator_5 (.a(in_1[31:26]), .b(6'b001101), .eq(ori));  // open: gt, lt
  Comparator #(.width(6)) comparator_6 (.a(in_1[31:26]), .b(6'b001110), .eq(xori));  // open: gt, lt
  or or_1 (MUL, mult, mulu);
  or or_2 (DIV, div_t, divu);
  or or_3 (SLT, slt_t, sltu);
  or or_4 (SLTI, slti_t, sltiu);
  or or_5 (jmp_inst, out_14, out_18, out_15, out_17, out_16, out_25, out_22, nop);
  or or_6 (R_inst, out_24, mflo, kbd, mfhi, out_23);
  or or_7 (ALU_inst, MUL, DIV, SLT, SLTI, AND, OR, XOR, ADD, \nor , sub);
  Comparator #(.width(6)) comparator_7 (.a(in_1[31:26]), .b(6'b100011), .eq(out_19));  // open: gt, lt
  Comparator #(.width(6)) comparator_8 (.a(in_1[31:26]), .b(6'b101011), .eq(out_13));  // open: gt, lt
  Comparator #(.width(6)) comparator_9 (.a(in_1[31:26]), .b(6'b000100), .eq(out_14));  // open: gt, lt
  Comparator #(.width(6)) comparator_10 (.a(in_1[31:26]), .b(6'b000101), .eq(out_15));  // open: gt, lt
  Comparator #(.width(6)) comparator_11 (.a(in_1[31:26]), .b(6'b000110), .eq(out_16));  // open: gt, lt
  Comparator #(.width(6)) comparator_12 (.a(in_1[31:26]), .b(6'b000111), .eq(out_17));  // open: gt, lt
  Comparator #(.width(6)) comparator_13 (.a(in_1[31:26]), .b(6'b000001), .eq(out_18));  // open: gt, lt
  or or_8 (out_9[0], out_19, out_20, mflo, kbd);
  or or_9 (out_9[1], mfhi, mflo);
  or or_10 (out_9[2], out_24, kbd);
  or or_11 (mem_inst, out_13, out_19);
  or or_12 (stack_inst, out_20, out_21);
  or or_13 (write_inst, out_13, out_21);
  or or_14 (AND, and_t, andi);
  or or_15 (OR, or_t, ori);
  or or_16 (XOR, xor_t, xori);
  or or_17 (ADD, add_t, addi);
  Comparator #(.width(6)) comparator_14 (.a(in_1[31:26]), .b(6'b000010), .eq(out_25));  // open: gt, lt
  or or_18 (out_10[0], R_inst, ALU_inst, write_inst);
  or or_19 (out_10[1], R_inst, jmp_inst);
  or or_20 (out_10[2], mem_inst, write_inst, stack_inst);
  Comparator #(.width(6)) comparator_15 (.a(in_1[31:26]), .b({6{1'b1}}), .eq(_111111));  // open: gt, lt
  Comparator #(.width(6)) comparator_16 (.a(in_1[31:26]), .b({6{1'b0}}), .eq(_000000));  // open: gt, lt
  Comparator #(.width(6)) comparator_17 (.a(in_1[5:0]), .b({6{1'b0}}), .eq(comparator_17_eq));  // open: gt, lt
  Comparator #(.width(6)) comparator_18 (.a(in_1[5:0]), .b(6'b100000), .eq(comparator_18_eq));  // open: gt, lt
  Comparator #(.width(6)) comparator_19 (.a(in_1[5:0]), .b(6'b100010), .eq(comparator_19_eq));  // open: gt, lt
  Comparator #(.width(6)) comparator_20 (.a(in_1[5:0]), .b(6'b011000), .eq(comparator_20_eq));  // open: gt, lt
  Comparator #(.width(6)) comparator_21 (.a(in_1[5:0]), .b(6'b011001), .eq(comparator_21_eq));  // open: gt, lt
  Comparator #(.width(6)) comparator_22 (.a(in_1[5:0]), .b(6'b011010), .eq(comparator_22_eq));  // open: gt, lt
  Comparator #(.width(6)) comparator_23 (.a(in_1[5:0]), .b(6'b011011), .eq(comparator_23_eq));  // open: gt, lt
  Comparator #(.width(6)) comparator_24 (.a(in_1[5:0]), .b(6'b101010), .eq(comparator_24_eq));  // open: gt, lt
  Comparator #(.width(6)) comparator_25 (.a(in_1[31:26]), .b(6'b111000), .eq(comparator_25_eq));  // open: gt, lt
  Comparator #(.width(6)) comparator_26 (.a(in_1[5:0]), .b({6{1'b0}}), .eq(comparator_26_eq));  // open: gt, lt
  Comparator #(.width(6)) comparator_27 (.a(in_1[31:26]), .b(6'b111000), .eq(comparator_27_eq));  // open: gt, lt
  Comparator #(.width(6)) comparator_28 (.a(in_1[5:0]), .b(6'b000001), .eq(comparator_28_eq));  // open: gt, lt
  and and_1 (out_3[31], in_1[15], ~ori, ~andi, ~xori);  // AND_Gate
  and and_2 (nop, _000000, comparator_17_eq);
  and and_3 (add_t, _000000, comparator_18_eq);
  and and_4 (sub, _000000, comparator_19_eq);
  and and_5 (mult, _000000, comparator_20_eq);
  and and_6 (mulu, _000000, comparator_21_eq);
  and and_7 (div_t, _000000, comparator_22_eq);
  and and_8 (divu, _000000, comparator_23_eq);
  and and_9 (slt_t, _000000, comparator_24_eq);
  and and_10 (out_20, comparator_25_eq, comparator_26_eq);
  and and_11 (out_21, comparator_27_eq, comparator_28_eq);
  Comparator #(.width(6)) comparator_29 (.a(in_1[5:0]), .b(6'b101011), .eq(comparator_29_eq));  // open: gt, lt
  Comparator #(.width(6)) comparator_30 (.a(in_1[5:0]), .b(6'b100100), .eq(comparator_30_eq));  // open: gt, lt
  Comparator #(.width(6)) comparator_31 (.a(in_1[5:0]), .b(6'b100101), .eq(comparator_31_eq));  // open: gt, lt
  Comparator #(.width(6)) comparator_32 (.a(in_1[5:0]), .b(6'b100111), .eq(comparator_32_eq));  // open: gt, lt
  Comparator #(.width(6)) comparator_33 (.a(in_1[5:0]), .b(6'b101000), .eq(comparator_33_eq));  // open: gt, lt
  Comparator #(.width(6)) comparator_34 (.a(in_1[5:0]), .b(6'b001000), .eq(comparator_34_eq));  // open: gt, lt
  Comparator #(.width(6)) comparator_35 (.a(in_1[5:0]), .b(6'b010000), .eq(comparator_35_eq));  // open: gt, lt
  Comparator #(.width(6)) comparator_36 (.a(in_1[5:0]), .b(6'b010010), .eq(comparator_36_eq));  // open: gt, lt
  Comparator #(.width(6)) comparator_37 (.a(in_1[5:0]), .b({6{1'b1}}), .eq(comparator_37_eq));  // open: gt, lt
  Comparator #(.width(6)) comparator_38 (.a(in_1[5:0]), .b(6'b000001), .eq(comparator_38_eq));  // open: gt, lt
  Comparator #(.width(6)) comparator_39 (.a(in_1[5:0]), .b(6'b000010), .eq(comparator_39_eq));  // open: gt, lt
  Comparator #(.width(6)) comparator_40 (.a(in_1[5:0]), .b(6'b000100), .eq(comparator_40_eq));  // open: gt, lt
  or or_21 (or_21_out, out_13, addi, out_19);
  and and_12 (sltu, _000000, comparator_29_eq);
  and and_13 (and_t, _000000, comparator_30_eq);
  and and_14 (or_t, _000000, comparator_31_eq);
  and and_15 (\nor , _000000, comparator_32_eq);
  and and_16 (xor_t, _000000, comparator_33_eq);
  and and_17 (out_22, _000000, comparator_34_eq);
  and and_18 (mfhi, _000000, comparator_35_eq);
  and and_19 (mflo, _000000, comparator_36_eq);
  and and_20 (halt, _111111, comparator_37_eq);
  and and_21 (out_23, _111111, comparator_38_eq);
  and and_22 (out_24, _111111, comparator_39_eq);
  and and_23 (kbd, _111111, comparator_40_eq);
  ALU_selector alu_selector_1 (
    .in_3(sub), .in_6(mult), .in_9(mulu), .in_12(div_t), .in_15(divu), .in_1(slt_t), .in_4(sltu),
    .in_7(and_t), .in_10(or_t), .in_13(\nor ), .in_16(xor_t), .in_2(or_21_out), .in_5(slti_t), .in_8(sltiu),
    .in_11(andi), .in_14(ori), .in_17(xori), .sign(out_11), .I(out_12), .selector(out_8));

  assign out_2 = in_1[25:0];
  assign out_3[30:0] = {{15{out_3[31]}}, in_1[15:0]};
  assign out_4 = in_1[15:0];
  assign out_5 = in_1[25:21];
  assign out_6 = in_1[20:16];
  assign out_7 = in_1[15:11];

  // Other names for the same wires on the sheet: ALU_selector[3:0] = out_8; beq = out_14; bgtz = out_17;
  //   blez = out_16; bltz = out_18; bne = out_15; constant__32[31:0] = {{16{out_3[31]}}, in_1[15:0]};
  //   CU_select[2:0] = out_10; I = out_12; constant[15:0] = in_1[15:0]; dest[25:0] = in_1[25:0]; FC[5:0] = in_1[5:0];
  //   RD[4:0] = in_1[15:11]; RT[4:0] = in_1[20:16]; RS[4:0] = in_1[25:21]; OP[5:0] = in_1[31:26]; j = out_25;
  //   jr = out_22; lw = out_19; pop = out_20; push = out_21; RF_INPUT_select[2:0] = out_9; rnd = out_24;
  //   sign = out_11; sw = out_13; tty = out_23

  // Notes on the sheet:
  //   Instrucciones Tipo I
  //   Control_Unit_Select
  //   Instrucciones Tipo J
  //   Instrucciones Tipo R
endmodule

module Data_Path_2 (
  input  [31:0] in_1,
  input  [6:0] in_2,
  input  in_3,
  input  in_4,
  input  in_5,
  input  in_6,
  input  in_7,
  input  in_8,
  output [31:0] Output,
  output [31:0] R_out,
  output [2:0] out_11,
  output [6:0] Output_2,
  output out_13
);

  wire beq, bgtz, blez, bltz, bne, I, j, jr, lw, pop, push, rnd, sign, sw;
  wire [2:0] RF_select;
  wire [3:0] ALU_selector;
  wire [4:0] multiplexer_2_out, RD, RS, RT;
  wire [15:0] \const ;
  wire [25:0] dest;
  wire [31:0] ALUout, branch_control_1_out_13, Const32, get_inst_1_output, HI, LO, multiplexer_1_out, PCout,
       random_1_out, rf_input_1_output, RT_t, SP;
  wire [31:7] RS_t;

  Multiplexer #(.width(32), .enable("false")) multiplexer_1 (
    .in0(RT_t), .in1(Const32), .out(multiplexer_1_out), .sel(I));
  ALU_2 alu_1 (
    .in_4(sign), .Input({RS_t, Output_2}), .Input_2(multiplexer_1_out), .in_3(ALU_selector), .out_6(ALUout),
    .out_7(LO), .out_8(HI), .in_5(in_5));
  Get_Inst get_inst_1 (.in_3(in_1), .Output(get_inst_1_output), .in_1(in_5), .in_2(in_6), .in_4(in_7));
  Branch_Control branch_control_1 (
    .in_1(dest), .in_2({RS_t, Output_2}), .in_3(RT_t), .in_4(PCout), .in_5(\const ), .in_6(beq), .in_7(bne),
    .in_8(blez), .in_9(bgtz), .in_10(bltz), .in_11(jr), .in_12(j), .out_13(branch_control_1_out_13));
  Program_Counter program_counter_1 (
    .in_1(in_5), .NEXT(branch_control_1_out_13), .in_2(in_4), .in_3(in_6), .out_5(PCout));
  Instruction_Decoder instruction_decoder_1 (
    .out_5(RS), .out_2(dest), .in_1(get_inst_1_output), .out_6(RT), .out_4(\const ), .out_7(RD), .out_13(sw),
    .out_14(beq), .out_15(bne), .out_16(blez), .out_17(bgtz), .out_18(bltz), .out_19(lw), .out_20(pop),
    .out_21(push), .out_23(out_13), .out_22(jr), .out_24(rnd), .out_25(j), .out_3(Const32),
    .out_8(ALU_selector), .out_9(RF_select), .out_10(out_11), .out_11(sign), .out_12(I));
  Random #(.width(32)) random_1 (.clk(in_5), .next(rnd), .out(random_1_out));  // open: clr
  Memory_Address memory_address_1 (
    .in_1(PCout), .in_2(ALUout), .in_3(SP), .in_4(lw), .in_6(pop), .in_8(in_8), .in_5(sw), .in_7(push),
    .out_9(Output));
  RF_Input rf_input_1 (
    .in_1(in_2), .in_2(ALUout), .in_3(RF_select), .in_4(random_1_out), .in_5(in_1), .in_6(HI), .in_7(LO),
    .Output(rf_input_1_output));
  Multiplexer #(.width(5), .enable("false")) multiplexer_2 (.in0(RD), .in1(RT), .out(multiplexer_2_out), .sel(I));
  Register_File register_file_1 (
    .in_10(in_6), .in_6(in_3), .in_7(push), .in_1(rf_input_1_output), .in_9(in_5), .in_5(in_4), .in_8(pop),
    .in_2(multiplexer_2_out), .in_3(RS), .in_4(RT), .out_11({RS_t, Output_2}), .out_12(RT_t), .out_13(SP));
  Multiplexer #(.width(32), .enable("false")) multiplexer_3 (.in0({RS_t, Output_2}), .in1(RT_t), .out(R_out), .sel(sw));

  // Other names for the same wires on the sheet: address[31:0] = Output; CLK = in_5; CLR = in_6;
  //   CU_select[2:0] = out_11; GNI = in_8; instruction[31:0] = in_1; KBDdata[6:0] = in_2; L_GI = in_7; L_PC = in_4;
  //   L_RF = in_3; RS_t[6:0] = Output_2; tty_data[6:0] = Output_2; tty = out_13
endmodule

module Get_Inst (
  input  in_1,
  input  in_2,
  input  [31:0] in_3,
  input  in_4,
  output [31:0] Output
);

  Register #(.width(32)) register_1 (
    .D(in_3), .en(in_4), .Q({Output[7:0], Output[15:8], Output[23:16], Output[31:24]}), .clk(in_1), .clr(in_2));

  // Other names for the same wires on the sheet: CLK = in_1; CLR = in_2; load = in_4
endmodule

module Memory_Address (
  input  [31:0] in_1,
  input  [31:0] in_2,
  input  [31:0] in_3,
  input  in_4,
  input  in_5,
  input  in_6,
  input  in_7,
  input  in_8,
  output [31:0] out_9
);

  wire [1:0] select;
  wire [31:0] multiplexer_1_out, subtractor_1_out;

  Subtractor #(.width(32)) subtractor_1 (.a(in_3), .b(32'h4), .out(subtractor_1_out));  // open: bin, bout
  or or_1 (select[0], in_4, in_8, in_5);
  or or_2 (select[1], in_7, in_8, in_6);
  Multiplexer #(.width(32), .enable("false")) multiplexer_1 (
    .in0(in_3), .in1(subtractor_1_out), .out(multiplexer_1_out), .sel(in_7));
  Multiplexer #(.select(2), .width(32), .enable("false")) multiplexer_2 (
    .in0(in_1), .in1(in_2), .in2(multiplexer_1_out), .in3(in_1), .out(out_9), .sel(select));

  // Other names for the same wires on the sheet: ALU[31:0] = in_2; GNI = in_8; lw = in_4; PC[31:0] = in_1; pop = in_6;
  //   push = in_7; SP[31:0] = in_3; sw = in_5
endmodule

module Program_Counter (
  input  in_1,
  input  in_2,
  input  in_3,
  input  [31:0] NEXT,
  output [31:0] out_5
);

  Register #(.width(32)) register_1 (.D(NEXT), .en(in_2), .Q(out_5), .clk(in_1), .clr(in_3));

  // Other names for the same wires on the sheet: CLK = in_1; CLR = in_3; load = in_2
endmodule

module Branch_Control (
  input  [25:0] in_1,
  input  [31:0] in_2,
  input  [31:0] in_3,
  input  [31:0] in_4,
  input  [15:0] in_5,
  input  in_6,
  input  in_7,
  input  in_8,
  input  in_9,
  input  in_10,
  input  in_11,
  input  in_12,
  output [31:0] out_13
);

  wire and_1_out, and_2_out, and_3_out, and_4_out, and_5_out, comparator_1_eq, or_2_out, RS_0, RS__0, RS__RT;
  wire [1:0] select;
  wire [13:0] bit_extender_1_out;
  wire [31:0] PC_4, PC_4_const;

  Comparator #(.width(32)) comparator_1 (.a(in_2), .b({32{1'b0}}), .eq(comparator_1_eq), .lt(RS_0));  // open: gt
  Comparator #(.width(32)) comparator_2 (.a(in_2), .b(in_3), .eq(RS__RT));  // open: gt, lt
  Adder #(.width(32)) adder_1 (.a(in_4), .b(32'h4), .out(PC_4));  // open: cin, cout
  assign bit_extender_1_out = {{13{in_5[15]}}, in_5[15]};  // Bit_Extender bit_extender_1
  or or_1 (RS__0, comparator_1_eq, RS_0);
  and and_1 (and_1_out, in_6, RS__RT);
  and and_2 (and_2_out, ~RS__RT, in_7);  // AND_Gate
  and and_3 (and_3_out, in_8, RS__0);
  and and_4 (and_4_out, ~RS__0, in_9);  // AND_Gate
  and and_5 (and_5_out, RS_0, in_10);
  Adder #(.width(32)) adder_2 (.a(PC_4), .b({bit_extender_1_out, in_5, 2'b00}), .out(PC_4_const));  // open: cin, cout
  or or_2 (or_2_out, and_1_out, and_2_out, and_3_out, and_4_out, and_5_out);
  or or_3 (select[0], or_2_out, in_11);
  or or_4 (select[1], in_11, in_12);
  Multiplexer #(.select(2), .width(32), .enable("false")) multiplexer_1 (
    .in0(PC_4), .in1(PC_4_const), .in2({in_4[31:28], in_1, 2'b00}), .in3(in_2), .out(out_13), .sel(select));

  // Other names for the same wires on the sheet: const[15:0] = in_5; beq = in_6; bgtz = in_9; blez = in_8;
  //   bltz = in_10; bne = in_7; j = in_12; dest[25:0] = in_1; jmp[31:2] = {in_4[31:28], in_1}; PC[31:0] = in_4;
  //   jr = in_11; RS[31:0] = in_2; RT[31:0] = in_3
endmodule

module Control_Unit (
  input  in_1,
  input  in_2,
  input  in_3,
  input  in_4,
  input  in_5,
  input  in_6,
  input  [2:0] in_7,
  input  in_8,
  output out_9,
  output out_10,
  output out_11,
  output out_12,
  output out_13,
  output out_14,
  output out_15,
  output out_16,
  output out_17
);

  wire branch, d_ff_1_q, d_ff_2_q, d_ff_3_q, d_ff_4_q, halt, or_3_out, RF, tunel;

  D_Flip_Flop #(.trigger("falling")) d_ff_1 (.clk(in_1), .D(in_4), .Q(d_ff_1_q), .reset(in_3));  // open: Qn, preset, en
  D_Flip_Flop #(.trigger("falling")) d_ff_2 (
    .clk(in_1), .D(tunel), .Q(d_ff_2_q), .reset(in_3));  // open: Qn, preset, en
  D_Flip_Flop #(.trigger("falling")) d_ff_3 (
    .clk(in_1), .D(out_11), .Q(d_ff_3_q), .reset(in_3));  // open: Qn, preset, en
  Demultiplexer #(.select(3), .enable("false")) demultiplexer_1 (
    .out0(halt), .out1(tunel), .out2(branch), .out3(RF), .out4(out_15), .out5(out_17), .in(d_ff_4_q),
    .sel(in_7));  // open: out6, out7
  D_Flip_Flop #(.trigger("falling")) d_ff_4 (.clk(in_1), .D(in_6), .Q(d_ff_4_q));  // open: Qn, preset, en, reset
  or or_1 (out_10, d_ff_1_q, d_ff_3_q);
  or or_2 (out_9, d_ff_2_q, in_5, RF);
  D_Flip_Flop #(.trigger("falling")) d_ff_5 (.clk(in_1), .D(out_9), .Q(out_16));  // open: Qn, preset, en, reset
  or or_3 (or_3_out, out_13, halt);
  D_Flip_Flop #(.trigger("falling")) d_ff_6 (
    .clk(in_1), .D(or_3_out), .Q(out_13), .reset(in_3));  // open: Qn, preset, en
  and and_1 (out_14, out_16, in_2);
  or or_4 (out_11, out_16, in_8, branch);

  assign out_12 = in_6;

  // Other names for the same wires on the sheet: CLK = in_1; CLR = in_3; cont = out_11; L_PC = out_11; end = out_13;
  //   get_data = out_15; get_inst = out_10; L_RF = out_9; L_tty = out_14; ready_data = in_5; L_GI = in_6;
  //   ready_inst = in_6; ready_w = in_8; select[2:0] = in_7; start = in_4; L_kbd = out_16; tty = out_16;
  //   tty_inst = in_2; write = out_17
endmodule

module Read_Write_RAM (
  input  [31:0] in_1,
  input  [31:0] in_2,
  input  [31:0] in_3,
  input  [31:0] in_4,
  input  [31:0] in_5,
  input  [3:0] in_6,
  input  [3:0] in_7,
  input  in_8,
  input  in_9,
  input  in_10,
  input  in_11,
  input  in_12,
  input  in_13,
  output [31:0] out_14,
  output [31:0] out_15,
  output [31:0] out_16,
  output [31:0] out_17,
  output [15:0] out_18,
  output [3:0] out_19,
  output out_20,
  output out_21,
  output out_22,
  output cs,
  output out_24
);

  wire CSD, CSI, or_1_out, stop;
  wire [31:0] DO0, DO1, DO2, DO3, IO0, IO1, IO2, IO3;

  read_RAM read_ram_1 (
    .in_1(in_1), .in_2(in_2), .in_3(in_3), .in_4(in_4), .in_5(in_6), .in_8(in_13), .in_6(in_8), .Output(IO0),
    .Output_2(IO1), .Output_3(IO2), .Output_4(IO3), .Output_6(CSI), .Output_5(out_20), .in_7(in_12));
  D_Flip_Flop #(.trigger("falling")) d_ff_1 (
    .clk(in_12), .D(in_10), .Q(out_24), .en(or_1_out));  // open: Qn, preset, reset
  or or_1 (or_1_out, in_10, stop);
  Cronometro cronometro_1 (.Enable(out_24), .CLR(out_22), .CLK(in_12), .Tiempo_de_espera(in_7), .out_5(stop));
  Demultiplexer #(.select(2), .enable("false")) demultiplexer_1 (
    .out0(out_19[0]), .out1(out_19[1]), .out2(out_19[2]), .out3(out_19[3]), .in(1'b1), .sel(in_5[3:2]));
  read_RAM read_ram_2 (
    .in_1(in_1), .in_2(in_2), .in_3(in_3), .in_4(in_4), .in_5(in_6), .in_8(in_13), .in_6(in_9), .Output(DO0),
    .Output_2(DO1), .Output_3(DO2), .Output_4(DO3), .Output_6(CSD), .Output_5(out_21), .in_7(in_12));
  D_Flip_Flop #(.trigger("falling")) d_ff_2 (.clk(in_12), .D(stop), .Q(out_22));  // open: Qn, preset, en, reset
  Multiplexer #(.width(32), .enable("false")) multiplexer_1 (
    .in0({DO0[7:0], DO0[15:8], DO0[23:16], DO0[31:24]}), .in1(IO0), .out(out_14), .sel(in_11));
  Multiplexer #(.width(32), .enable("false")) multiplexer_2 (
    .in0({DO1[7:0], DO1[15:8], DO1[23:16], DO1[31:24]}), .in1(IO1), .out(out_15), .sel(in_11));
  Multiplexer #(.width(32), .enable("false")) multiplexer_3 (
    .in0({DO2[7:0], DO2[15:8], DO2[23:16], DO2[31:24]}), .in1(IO2), .out(out_16), .sel(in_11));
  Multiplexer #(.width(32), .enable("false")) multiplexer_4 (
    .in0({DO3[7:0], DO3[15:8], DO3[23:16], DO3[31:24]}), .in1(IO3), .out(out_17), .sel(in_11));
  or or_2 (cs, CSD, CSI, out_24);

  assign out_18 = in_5[19:4];

  // Other names for the same wires on the sheet: bank0[31:0] = in_1; bank1[31:0] = in_2; bank2[31:0] = in_3;
  //   bank3[31:0] = in_4; CLK = in_12; DP_address[31:0] = in_5; address[15:0] = in_5[19:4]; get_data = in_9;
  //   get_inst = in_8; is_inst = in_11; mask[3:0] = out_19; read_time[3:0] = in_6; ready_data = out_21;
  //   ready_inst = out_20; ready_write = out_22; reset = in_13; RW = out_24; write = in_10; write_time[3:0] = in_7

  // Notes on the sheet:
  //   como para escribir en la RAM no necesitamos guardar lo q se va a escribir en un registro  no lo hacemos con el READ RAM, sin embargo se hace analogo a este
endmodule

module read_RAM (
  input  [31:0] in_1,
  input  [31:0] in_2,
  input  [31:0] in_3,
  input  [31:0] in_4,
  input  [3:0] in_5,
  input  in_6,
  input  in_7,
  input  in_8,
  output [31:0] Output,
  output [31:0] Output_2,
  output [31:0] Output_3,
  output [31:0] Output_4,
  output Output_5,
  output Output_6
);

  wire enable, Mantener_q, or_1_out, stop;

  Register #(.width(32)) register_1 (.D(in_1), .en(enable), .Q(Output), .clk(in_7), .clr(in_8));
  D_Flip_Flop #(.trigger("falling")) Mantener (
    .clk(in_7), .D(in_6), .Q(Mantener_q), .en(or_1_out));  // open: Qn, preset, reset
  or or_1 (or_1_out, in_6, stop);
  Register #(.width(32)) register_2 (.D(in_2), .en(enable), .Q(Output_2), .clk(in_7), .clr(in_8));
  Cronometro cronometro_1 (.Enable(Mantener_q), .CLR(Output_5), .CLK(in_7), .Tiempo_de_espera(in_5), .out_5(stop));
  Register #(.width(32)) register_3 (.D(in_3), .en(enable), .Q(Output_3), .clk(in_7), .clr(in_8));
  D_Flip_Flop #(.trigger("falling")) Espera (
    .clk(in_7), .D(stop), .Q(enable), .reset(Output_5));  // open: Qn, preset, en
  D_Flip_Flop #(.trigger("falling")) Terminar (.clk(in_7), .D(enable), .Q(Output_5));  // open: Qn, preset, en, reset
  or or_2 (Output_6, enable, Mantener_q);
  Register #(.width(32)) register_4 (.D(in_4), .en(enable), .Q(Output_4), .clk(in_7), .clr(in_8));

  // Other names for the same wires on the sheet: bank0[31:0] = in_1; bank1[31:0] = in_2; bank2[31:0] = in_3;
  //   bank3[31:0] = in_4; clock = in_7; CS = Output_6; get = in_6; out_bank0[31:0] = Output;
  //   out_bank1[31:0] = Output_2; out_bank2[31:0] = Output_3; out_bank3[31:0] = Output_4; read_time[3:0] = in_5;
  //   ready = Output_5; reset = in_8

  // Notes on the sheet:
  //   como el get entra solo un ciclo 'Mantener'  va a estar sacando 1 hasta que se active el stop
  //   al mismo tiempo que esatn entrando los valores por los bank se activa el enable q es salida de Espera 
  //   como el stop no se prende hasta q termina el Crono => el CS va estar prendido todo el tiempo q el crono este funcionando
  //   al pasar un ciclo el espera va a sacar 1,por lo q el CS aun sigue prendido y como ya paso el RT por los bank0,...,bank3 estaran entrando los valores q se querian leer
  //   por lo q al pasar un ciclo ya van a estar guardados en los registros asignados yTerminar va a sacar 1 , por lo q se resetea el Crono y terminaria el circuito
endmodule

module Cronometro (
  input  [3:0] Tiempo_de_espera,
  input  Enable,
  input  CLK,
  input  CLR,
  output out_5
);

  wire [3:0] counter_1_q;

  Counter #(.width(4), .max('hf)) counter_1 (
    .count(Enable), .Q(counter_1_q), .clk(CLK), .clr(CLR));  // open: load, D, carry
  Comparator #(.width(4)) comparator_1 (.a(Tiempo_de_espera), .b(counter_1_q), .eq(out_5));  // open: gt, lt
endmodule
